# Fritzing sketch Garduino (saved by Fritzing 0.9.8b)
breadboards: 1

parts:
  Part1 = Arduino Uno (Rev3)
  Part2 = Soil Moisture Sensor
  Part3 = MAX7219 8x8 LedMatrix Module [part_number=DISPLAY]
  Q1 = NPN-Transistor [part_number=2222a package="SOT-23 [SMD]"]
  M1 = DC Motor [part_number="POMPA APA"]

nets:
  N1: Part1.D11_PWM/MOSI, Part3.CS
  N2: Part1.D12/MISO, Part3.DIN
  N3: Part1.D13/SCK, Part3.CLK
  N4: Part1.D2, Q1.0
  N5: Part1.D4, Part2.SIG
  VCC: Part1.5V, Part2.VCC, Part3.VCC, Q1.2
  GND: Part2.GND, Part3.GND, M1.pin_2
  N6: Q1.1, M1.pin_1

notes:
  Pompa de apa

custom parts:
  MAX7219 8x8 LedMatrix Module: Description: MAX7219 8x8 LedMatrix Red Module Dimensions: 32x32mm Documents:
